# Fritzing sketch Motor driver 8833 4 (saved by Fritzing 0.9.6b)

parts:
  U3 = DRV8833
  U1 = Mini-360 DC-DC Buck converter [package=THT]
  D1 = Rectifier Diode [part_number=1N4001 package="300 mil [THT]"]
  JP8 = Header 1 [package=1x01_offset]
  JP9 = Header 1 [package=1x01_offset]
  JP10 = Header 1 [package=1x01_offset]
  JP7 = Header 1 [package=1x01_offset]
  JP1 = Header 1 [package=1x01_offset]
  JP11 = Header 1 [package=1x01_offset]
  U2 = Arduino Pro Mini V2 (5V)
  SCL = Header 1 [package=1x01_offset]
  SDA = Header 1 [package=1x01_offset]
  R1 = Resistor [tolerance=±5% power=0.25W resistance=10k package=THT]
  R2 = Resistor [tolerance=±5% power=0.25W resistance=10k package=THT]
  C1 = Ceramic Capacitor [capacitance=0.27nF voltage=35V package="100 mil [THT, multilayer]"]
  C2 = Ceramic Capacitor [capacitance=0.27nF voltage=35V package="100 mil [THT, multilayer]"]
  Encoder_B = Header 1 [package=1x01_offset]
  Encoder_A = Header 1 [package=1x01_offset]

nets:
  GND: U3.GND, U1.IN-, U1.OUT-, D1.anode, JP11.1, U2.GND, C1.1, C2.0
  N1: U3.IN1_(AIN1), U2.D9
  N2: U3.IN2_(AIN2), U2.D3
  9V: U3.VCC, U1.IN+, D1.cathode, JP1.1
  N3: U3.OUT1_(AOUT1), JP7.1
  N4: U3.OUT2_(AOUT2), JP8.1
  N5: U3.OUT3_(BOUT1), JP9.1
  N6: U3.OUT4_(BOUT2), JP10.1
  N7: U3.IN3_(BIN1), U2.D5
  N8: U3.IN4_(BIN2), U2.D6
  5V: U1.OUT+, U2.VCC, R1.Pin_1, R2.Pin_1
  N9: U2.A4, SDA.1
  N10: U2.A5, SCL.1
  N11: U2.A1, R2.Pin_0, C1.0, Encoder_B.1
  N12: U2.A0, R1.Pin_0, C2.1, Encoder_A.1

custom parts:
  DRV8833: The DRV8833 provides a dual bridge motor driver solution for toys, printers, and other mechatronic applications.
  Mini-360 DC-DC Buck converter: Mini-360 DC-DC Buck converter. Tiny buck step down voltage converter, input voltage 4.75 to 23V output 1 to 17V adjustable. Available from ebay and the like.
  Arduino Pro Mini V2 (5V): Arduino Pro Mini V2 There are several different layouts for this board out there. This one is modeled after the Sparkfun 11113 board but a few of the pins have been moved around.
