# Fritzing sketch Motor driver 8833 (saved by Fritzing 0.9.6b)
stripboards: 3

parts:
  U3 = DRV8833
  U1 = Mini-360 DC-DC Buck converter [package=THT]
  D1 = Rectifier Diode [part_number=1N4001 package="300 mil [THT]"]
  Motor_1_B = Header 1 [package=1x01_offset]
  Motor_2_A = Header 1 [package=1x01_offset]
  Motor_2_B = Header 1 [package=1x01_offset]
  Motor_1_A = Header 1 [package=1x01_offset]
  9V = Header 1 [package=1x01_offset]
  GND = Header 1 [package=1x01_offset]
  U2 = Arduino Pro Mini V2 (5V)
  SCL = Header 1 [package=1x01_offset]
  SDA = Header 1 [package=1x01_offset]
  R1 = Resistor [tolerance=±5% power=0.25W resistance=10k package=THT]
  R2 = Resistor [tolerance=±5% power=0.25W resistance=10k package=THT]
  C1 = Ceramic Capacitor [capacitance=0.33nF voltage=35V package="100 mil [THT, multilayer]"]
  C2 = Ceramic Capacitor [capacitance=0.33nF voltage=35V package="100 mil [THT, multilayer]"]
  Encoder_A = Header 1 [package=1x01_offset]
  Limit_A_1 = Header 1 [package=1x01_offset]
  Limit_B_1 = Header 1 [package=1x01_offset]
  Limit_B_2 = Header 1 [package=1x01_offset]
  Limit_A_2 = Header 1 [package=1x01_offset]
  Servo_2 = Dagu DGServo 9g header (male) [package=THT]
  Servo_1 = Dagu DGServo 9g header (male) [package=THT]
  Encoder_B = Header 1 [package=1x01_offset]
  Encoder_A1 = Header 1 [package=1x01_offset]
  Encoder_A2 = Header 1 [package=1x01_offset]
  Encoder_A3 = Header 1 [package=1x01_offset]
  Encoder_A4 = Header 1 [package=1x01_offset]
  GND_2 = Header 1 [package=1x01_offset]
  GND_3 = Header 1 [package=1x01_offset]
  GND_4 = Header 1 [package=1x01_offset]
  R5 = Resistor [tolerance=±5% resistance=10k package="1206 [SMD]"]
  Message = Header 1 [package=1x01_offset]
  Address_select2 = Header 1 [package=1x01_offset]
  Address_select1 = Header 1 [package=1x01_offset]
  Q1 = NPN-Transistor [package="TO92 [THT]"]

nets:
  GND: U3.GND, U1.IN-, U1.OUT-, D1.anode, GND.1, U2.GND, C1.1, C2.0, Servo_2.gnd, Servo_1.gnd, Encoder_A3.1, Encoder_A4.1, GND_2.1, GND_3.1, GND_4.1, Q1.E
  N1: U3.IN1_(AIN1), U2.D9
  N2: U3.IN2_(AIN2), U2.D3
  9V: U3.VCC, U1.IN+, D1.cathode, 9V.1, U2.RAW
  N3: U3.OUT1_(AOUT1), Motor_1_A.1
  N4: U3.OUT2_(AOUT2), Motor_1_B.1
  N5: U3.OUT3_(BOUT1), Motor_2_A.1
  N6: U3.OUT4_(BOUT2), Motor_2_B.1
  N7: U3.IN3_(BIN1), U2.D5
  N8: U3.IN4_(BIN2), U2.D6
  4.8V: U1.OUT+, Servo_2.Vcc, Servo_1.Vcc
  N9: U2.A4, SDA.1
  N10: U2.A5, SCL.1
  5V: U2.VCC, R1.Pin_1, R2.Pin_1, Encoder_A1.1, Encoder_A2.1
  N11: U2.A3, Limit_B_2.1
  N12: U2.A2, Limit_B_1.1
  N13: U2.A1, R2.Pin_0, C1.0, Encoder_B.1
  N14: U2.A0, R1.Pin_0, C2.1, Encoder_A.1
  N15: U2.SCK, R5.Pin_0
  N16: U2.MOSI, Servo_2.pulse
  N17: U2.D10, Servo_1.pulse
  N18: U2.D8, Limit_A_1.1
  N19: U2.D7, Limit_A_2.1
  N20: U2.D4, Address_select2.1
  N21: U2.D2, Address_select1.1
  N22: R5.Pin_1, Q1.B
  N23: Message.1, Q1.C

custom parts:
  DRV8833: The DRV8833 provides a dual bridge motor driver solution for toys, printers, and other mechatronic applications.
  Mini-360 DC-DC Buck converter: Mini-360 DC-DC Buck converter. Tiny buck step down voltage converter, input voltage 4.75 to 23V output 1 to 17V adjustable. Available from ebay and the like.
  Arduino Pro Mini V2 (5V): Arduino Pro Mini V2 There are several different layouts for this board out there. This one is modeled after the Sparkfun 11113 board but a few of the pins have been moved around.
