# Fritzing sketch Test setup 2 (saved by Fritzing 0.9.6b)
breadboards: 1

parts:
  IC2 = L293D [package=THT]
  IC1 = Arduino Nano (Rev3.0)
  C1 = Capacitor [package=cap-pth-small-kit]
  C2 = Capacitor [package=cap-pth-small-kit]
  C4 = Capacitor [package=cap-pth-small-kit]
  R2 = Resistor [tolerance=±5% resistance=10k package="1206 [SMD]"]
  C3 = Capacitor [package=cap-pth-small-kit]
  R3 = Resistor [tolerance=±5% resistance=10k package="1206 [SMD]"]
  micro_bit_(external_controller) = Microbit
  U1 = Voltage Regulator - 5V [package="TO220 [THT]"]
  Limit_B1 = Round Pushbutton
  Limit_A1 = Round Pushbutton
  Limit_A2 = Round Pushbutton
  Q1 = NPN-Transistor [package="TO92 [THT]"]
  R3_2 = Resistor [tolerance=±5% resistance=1k package="1206 [SMD]"]
  J1_(9_VDC) = Power Jack [package=power_jack_pth]
  LED1 = LED - 3mm [color="Yellow (595nm)" current=0.030 package="3 mm [THT]"]
  LED2 = LED - 3mm [color="Blue (505nm)" current=0.030 package="3 mm [THT]"]
  Motor_A = DC Motor
  Motor_B_(encoder) = DC Motor with two-phase hall-encoder [part_number=VT-E-G25A-06-177E]
  R1 = Resistor [tolerance=±5% resistance=1k package="1206 [SMD]"]

nets:
  5V: IC2.Enable_1, IC2.Enable_2, IC1.5V, R2.Pin_0, U1.output_voltage, R3_2.Pin_0, Motor_B_(encoder).pin4
  N1: IC2.In_1, IC1.D5
  N2: IC2.Out_1_(_Controlled_by_Enable_1_), C1.1, Motor_A.pin_1
  GND: IC2.0V, IC1.GND, C1.2, C2.1, C4.1, C3.2, micro_bit_(external_controller).GND, U1.GND, Limit_B1.leg0, Limit_A1.leg0, Limit_A2.leg0, Q1.E, J1_(9_VDC).GND, Motor_B_(encoder).pin3, R1.Pin_1
  N3: IC2.Out_2_(_Controlled_by_Enable_1_), C2.2, Motor_A.pin_2
  N4: IC2.In_2, IC1.D6
  N5: IC2.+Vmotor, IC2.+V, U1.input_voltage, J1_(9_VDC).PWR, LED1.anode
  N6: IC2.In_3, IC1.D3
  N7: IC2.Out_3_(_Controlled_by_Enable_2_), C4.2, Motor_B_(encoder).pin1
  N8: IC2.Out_4_(_Controlled_by_Enable_2_), C3.1, Motor_B_(encoder).pin6
  N9: IC2.In_4, IC1.D9
  N10: IC1.D2, R2.Pin_1, Motor_B_(encoder).pin5
  N11: IC1.A5, micro_bit_(external_controller).P19
  N12: IC1.A4, micro_bit_(external_controller).P20
  N13: IC1.A3, Limit_A2.leg1
  N14: IC1.A2, Limit_A1.leg1
  N15: IC1.A0, Limit_B1.leg1
  N16: IC1.D13/SCK, R3.Pin_0
  N17: R3.Pin_1, Q1.B
  N18: micro_bit_(external_controller).P12, Q1.C, LED2.cathode
  N19: R3_2.Pin_1, LED2.anode
  N20: LED1.cathode, R1.Pin_0

custom parts:
  Microbit: BBC Microbit Fritzing part. May 2019 expanded to include schematic and pcb views as well as breadboard. PCB view assumes an Adafruit PRODUCT ID: 3342 2x40 Right Angle through hole edge connector (although others will probably work as well). The pcb svg is custom (see forum article http://forum.fritzing.org/t/making-edge-connectors-and-both-side-smd-parts/7287 for an explaination if you need to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
